// Logisim project bodicky-riesenie34.circ as structural Verilog: 1 circuit, main circuit main
module main (
  input  A,
  input  B,
  input  C,
  input  D,
  output Y,
  output Z,
  output Y_DNF,
  output Z_DNF,
  output Y_KNF,
  output Z_KNF
);

  wire and_1_out, and_2_out, and_3_out, and_4_out, and_5_out, and_6_out, nand_1_out, nor_1_out, not_1_out,
       not_2_out, not_3_out, not_4_out, not_5_out, not_6_out, not_7_out, not_8_out, not_9_out, not_10_out,
       not_11_out, or_1_out, or_2_out, or_3_out, or_4_out, or_5_out, or_6_out;

  and and_1 (and_1_out, A, B);
  nor nor_1 (nor_1_out, C, not_1_out);
  not not_1 (not_1_out, D);
  nand nand_1 (nand_1_out, B, D);
  not not_2 (not_2_out, A);
  or or_1 (or_1_out, not_2_out, not_3_out);
  not not_3 (not_3_out, B);
  or or_2 (or_2_out, C, not_4_out);
  not not_4 (not_4_out, D);
  not not_5 (not_5_out, B);
  and and_2 (and_2_out, not_5_out, not_6_out);
  not not_6 (not_6_out, C);
  and and_3 (and_3_out, B, C);
  not not_7 (not_7_out, A);
  or or_3 (or_3_out, not_7_out, not_8_out);
  not not_8 (not_8_out, B);
  or or_4 (or_4_out, C, not_9_out);
  not not_9 (not_9_out, D);
  or or_5 (or_5_out, B, not_10_out);
  not not_10 (not_10_out, C);
  not not_11 (not_11_out, B);
  or or_6 (or_6_out, not_11_out, C);
  nand nand_2 (Y, and_1_out, nor_1_out);
  xnor xnor_1 (Z, nor_1_out, nand_1_out);
  or or_7 (Y_DNF, or_1_out, or_2_out);
  and and_4 (and_4_out, and_2_out, D);
  and and_5 (and_5_out, and_3_out, D);
  or or_8 (Y_KNF, or_3_out, or_4_out);
  and and_6 (and_6_out, or_5_out, or_6_out);
  or or_9 (Z_DNF, and_4_out, and_5_out);
  and and_7 (Z_KNF, and_6_out, D);
endmodule
