// Logisim project riesenie34.circ as structural Verilog: 1 circuit, main circuit main
module main (
  input  A,
  input  B,
  input  C,
  input  D,
  output Y,
  output Z,
  output Y_DNF,
  output Z_DNF,
  output Y_KNF,
  output Z_KNF
);

  wire and_1_out, and_2_out, and_3_out, nand_1_out, nor_1_out, not_1_out, not_2_out, not_3_out, not_4_out,
       not_5_out, not_6_out, not_7_out, not_8_out, not_9_out, not_10_out, not_11_out, or_2_out, or_3_out;

  and and_1 (and_1_out, A, B);
  nor nor_1 (nor_1_out, C, not_1_out);
  not not_1 (not_1_out, D);
  nand nand_1 (nand_1_out, B, D);
  not not_2 (not_2_out, A);
  not not_3 (not_3_out, B);
  not not_4 (not_4_out, D);
  not not_5 (not_5_out, B);
  not not_6 (not_6_out, C);
  and and_2 (and_2_out, not_5_out, not_6_out, D);
  and and_3 (and_3_out, B, C, D);
  not not_7 (not_7_out, A);
  not not_8 (not_8_out, B);
  or or_1 (Y_KNF, not_7_out, not_8_out, C, not_9_out);
  not not_9 (not_9_out, D);
  or or_2 (or_2_out, B, not_10_out);
  not not_10 (not_10_out, C);
  not not_11 (not_11_out, B);
  or or_3 (or_3_out, not_11_out, C);
  nand nand_2 (Y, and_1_out, nor_1_out);
  xnor xnor_1 (Z, nor_1_out, nand_1_out);
  or or_4 (Y_DNF, not_2_out, not_3_out, C, not_4_out);
  or or_5 (Z_DNF, and_2_out, and_3_out);
  and and_4 (Z_KNF, or_2_out, or_3_out, D);
endmodule
