// Logisim project riesenie.circ as structural Verilog: 1 circuit, main circuit main
module main (
  input  a,
  input  b,
  input  c,
  input  d,
  output A_D,
  output B_D,
  output C_D,
  output D_D,
  output A_K,
  output B_K,
  output C_K,
  output D_K
);

  wire na_2_out, na_out, nand_1_out, nand_2_out, nand_3_out, nand_4_out, nand_5_out, nand_6_out, nand_7_out,
       nb_2_out, nb_out, nc_2_out, nc_out, nor_1_out, nor_2_out, nor_3_out, nor_4_out, nor_5_out, nor_6_out,
       nor_7_out;

  nand na (na_out, a, a);
  nor na_2 (na_2_out, a, a);
  nand nb (nb_out, b, b);
  nand nc (nc_out, c, c);
  nor nb_2 (nb_2_out, b, b);
  nor nc_2 (nc_2_out, c, c);
  nand nd (D_D, d, d);
  nor nd_2 (D_K, d, d);
  nand nand_1 (nand_1_out, b, c);
  nand nand_2 (nand_2_out, b, d);
  nand nand_3 (nand_3_out, nb_out, c);
  nand nand_4 (nand_4_out, nb_out, d);
  nand nand_5 (nand_5_out, b, nc_out, D_D);
  nand nand_6 (nand_6_out, c, d);
  nand nand_7 (nand_7_out, nc_out, D_D);
  nor nor_1 (nor_1_out, a, b);
  nor nor_2 (nor_2_out, a, c, d);
  nor nor_3 (nor_3_out, nb_2_out, nc_2_out);
  nor nor_4 (nor_4_out, nb_2_out, D_K);
  nor nor_5 (nor_5_out, b, c, d);
  nor nor_6 (nor_6_out, c, D_K);
  nor nor_7 (nor_7_out, nc_2_out, d);
  nand nand_8 (A_D, na_out, nand_1_out, nand_2_out);
  nand nand_9 (B_D, nand_3_out, nand_4_out, nand_5_out);
  nand nand_10 (C_D, nand_6_out, nand_7_out);
  nor nor_8 (A_K, nor_1_out, nor_2_out);
  nor nor_9 (B_K, nor_3_out, nor_4_out, nor_5_out);
  nor nor_10 (C_K, nor_6_out, nor_7_out);
endmodule
