// Logisim project bodicky.circ as structural Verilog: 3 circuits, main circuit main
module main (
  input  RESET,
  input  START_STOP,
  output Z1,
  output Z2,
  output Z3,
  output Y_MOORE,
  output Z1_2,
  output Z2_2,
  output Z3_2,
  output Y_MEALY
);

  wire and_1_out, CLOCK_out, CLOCK_prime_out, rom_1_data;
  wire [4:0] counter_1_q;

  Clock CLOCK (.out(CLOCK_out));
  and and_1 (and_1_out, START_STOP, CLOCK_out);
  Counter #(.width(5), .max('h1f)) counter_1 (
    .Q(counter_1_q), .clk(and_1_out), .clr(RESET));  // open: load, D, count, carry
  not CLOCK_prime (CLOCK_prime_out, and_1_out);
  ROM #(.addrWidth(5), .dataWidth(1)) rom_1 (.addr(counter_1_q), .data(rom_1_data));  // open: sel
  Moore moore_1 (.Y(Y_MOORE), .RST(RESET), .CLK(CLOCK_prime_out), .X(rom_1_data), .Z1(Z1), .Z2(Z2), .Z3(Z3));
  Mealy mealy_1 (.RST(RESET), .CLK(CLOCK_prime_out), .X(rom_1_data), .Y(Y_MEALY), .Z1(Z1_2), .Z2(Z2_2), .Z3(Z3_2));

  // Notes on the sheet:
  //   RESET - restuje obvod
  //   CLOCK - synchronizačná premenná
  //   START/STOP - pozastaví načítavanie X do automatov
  //   Pre správne spustenie simuácie je potrebné
  //   mať zapnuté nastavenie Simulate->Simulation Enabled 
  //   a tiež nastaviť Simulate->Tick Frequency> 1Hz a následne
  //   Simulate->Ticks Enabled. Pre odskúšanie obvodu som už
  //   nastavil ROM na nejaké hodnoty ktoré rôznym spôsobom
  //   otestujú funkčnosť obvodu. Pre ručné otestovanie obvodu
  //   je možné v ľavom menu si otvoriť daný automat a zadávať X ručne.
  //   contents of rom_1 (hex, n*v repeats v):
  //   1 1 4*0 1 4*0 1 0 0 1 0 0 0 1 1 4*0 1 1 1 4*0 1
  //   lebo hodnota s ROM bola naraz načítaná z pamäte spolu so
  //   Pri kliknutí Poke Tool(hnedá ruka) na obvod sa zobrazí uprostred lupa
  //   na ktorú keď sa kline počas automatickej simulácie, tak je možné
  //   sledovať ako prebieha daná simulácia vo vnútri obvodu.
  //   Pre správnu funkčnosť obvodu som musel pridať negáciu CLOCK'
  //   zápisom do JK-PO. Toto spôsobovalo chybo že nebola zapisovaná
  //   aktuálne načítaná hodnota z pamäte, ale predchádzajúca hodnota.
  //   Pre jednoduchšie sledovanie stavu v ktorom
  //   sa JK-PO vo vnútri automatu nachádzajú, som pridal
  //   okrem výstupu Y aj výstupy Z1, Z2 a Z3.
endmodule

module Moore (
  input  RST,
  input  CLK,
  input  X,
  output Z1,
  output Z2,
  output Z3,
  output Y
);

  wire JK1_qn, JK2_qn, JK3_qn, nand_1_out, nand_2_out, nand_3_out, nand_4_out, nand_5_out, nand_7_out,
       nand_8_out, nand_9_out, nand_10_out, nand_11_out;

  nand nand_1 (nand_1_out, X, X);
  nand nand_2 (nand_2_out, Z2, JK3_qn);
  nand nand_3 (nand_3_out, nand_1_out, JK1_qn, JK2_qn, Z3);
  nand nand_4 (nand_4_out, X, JK1_qn);
  nand nand_5 (nand_5_out, nand_1_out, Z1, JK2_qn);
  nand nand_6 (Y, nand_2_out, nand_2_out);
  nand nand_7 (nand_7_out, nand_3_out, nand_3_out);
  nand nand_8 (nand_8_out, nand_1_out, Z3);
  nand nand_9 (nand_9_out, nand_3_out, nand_1_out);
  nand nand_10 (nand_10_out, nand_4_out, JK2_qn);
  nand nand_11 (nand_11_out, nand_5_out, nand_5_out);
  J_K_Flip_Flop JK1 (.J(nand_7_out), .clk(CLK), .K(nand_8_out), .Q(Z1), .Qn(JK1_qn), .reset(RST));  // open: preset, en
  J_K_Flip_Flop JK2 (.J(nand_9_out), .clk(CLK), .K(nand_1_out), .Q(Z2), .Qn(JK2_qn), .reset(RST));  // open: preset, en
  J_K_Flip_Flop JK3 (
    .J(nand_10_out), .clk(CLK), .K(nand_11_out), .Q(Z3), .Qn(JK3_qn), .reset(RST));  // open: preset, en
endmodule

module Mealy (
  input  RST,
  input  CLK,
  input  X,
  output Z1,
  output Z2,
  output Z3,
  output Y
);

  wire JK1_qn, JK2_qn, JK3_qn, nand_1_out, nand_2_out, nand_3_out, nand_4_out, nand_5_out, nand_7_out,
       nand_8_out, nand_9_out, nand_10_out, nand_11_out;

  nand nand_1 (nand_1_out, X, X);
  nand nand_2 (nand_2_out, X, Z1, JK2_qn);
  nand nand_3 (nand_3_out, nand_1_out, Z3);
  nand nand_4 (nand_4_out, nand_1_out, Z1, JK3_qn);
  nand nand_5 (nand_5_out, nand_1_out, JK1_qn, Z2);
  nand nand_6 (Y, nand_2_out, nand_2_out);
  nand nand_7 (nand_7_out, nand_3_out, nand_3_out);
  nand nand_8 (nand_8_out, nand_1_out, Z2);
  nand nand_9 (nand_9_out, nand_4_out, nand_4_out);
  nand nand_10 (nand_10_out, nand_5_out, nand_5_out);
  nand nand_11 (nand_11_out, nand_1_out, JK1_qn);
  J_K_Flip_Flop JK1 (.J(nand_7_out), .clk(CLK), .K(nand_8_out), .Q(Z1), .Qn(JK1_qn), .reset(RST));  // open: preset, en
  J_K_Flip_Flop JK2 (.J(X), .clk(CLK), .K(nand_9_out), .Q(Z2), .Qn(JK2_qn), .reset(RST));  // open: preset, en
  J_K_Flip_Flop JK3 (
    .J(nand_10_out), .clk(CLK), .K(nand_11_out), .Q(Z3), .Qn(JK3_qn), .reset(RST));  // open: preset, en
endmodule
