// Logisim project riesenie.circ as structural Verilog: 3 circuits, main circuit main
module main (
  input  [15:0] X,
  input  RESET,
  input  START_STOP,
  output Y_MOORE,
  output Y_MEALY
);

  wire and_1_out, bitselector_1_out, CLOCK_out;
  wire [3:0] counter_1_q;

  Clock CLOCK (.out(CLOCK_out));
  and and_1 (and_1_out, START_STOP, CLOCK_out);
  BitSelector #(.width(16)) bitselector_1 (.in(X), .out(bitselector_1_out), .sel(counter_1_q));
  Counter #(.width(4), .max('hf)) counter_1 (
    .Q(counter_1_q), .clk(and_1_out), .clr(RESET));  // open: load, D, count, carry
  Moore moore_1 (.Y(Y_MOORE), .RST(RESET), .CLK(and_1_out), .X(bitselector_1_out));
  Mealy mealy_1 (.RST(RESET), .CLK(and_1_out), .X(bitselector_1_out), .Y(Y_MEALY));
endmodule

module Moore (
  input  RST,
  input  CLK,
  input  X,
  output Y
);

  wire JK1_q, JK1_qn, JK2_q, JK2_qn, JK3_q, JK3_qn, nand_1_out, nand_2_out, nand_3_out, nand_4_out,
       nand_5_out, nand_7_out, nand_8_out, nand_9_out, nand_10_out, nand_11_out;

  nand nand_1 (nand_1_out, X, X);
  nand nand_2 (nand_2_out, JK2_q, JK3_qn);
  nand nand_3 (nand_3_out, nand_1_out, JK1_qn, JK2_qn, JK3_q);
  nand nand_4 (nand_4_out, X, JK1_qn);
  nand nand_5 (nand_5_out, nand_1_out, JK1_q, JK2_qn);
  nand nand_6 (Y, nand_2_out, nand_2_out);
  nand nand_7 (nand_7_out, nand_3_out, nand_3_out);
  nand nand_8 (nand_8_out, nand_1_out, JK3_q);
  nand nand_9 (nand_9_out, nand_3_out, nand_1_out);
  nand nand_10 (nand_10_out, nand_4_out, JK2_qn);
  nand nand_11 (nand_11_out, nand_5_out, nand_5_out);
  J_K_Flip_Flop JK1 (
    .J(nand_7_out), .clk(CLK), .K(nand_8_out), .Q(JK1_q), .Qn(JK1_qn), .reset(RST));  // open: preset, en
  J_K_Flip_Flop JK2 (
    .J(nand_9_out), .clk(CLK), .K(nand_1_out), .Q(JK2_q), .Qn(JK2_qn), .reset(RST));  // open: preset, en
  J_K_Flip_Flop JK3 (
    .J(nand_10_out), .clk(CLK), .K(nand_11_out), .Q(JK3_q), .Qn(JK3_qn), .reset(RST));  // open: preset, en
endmodule

module Mealy (
  input  RST,
  input  CLK,
  input  X,
  output Y
);

  wire JK1_q, JK1_qn, JK2_q, JK2_qn, JK3_q, JK3_qn, nand_1_out, nand_2_out, nand_3_out, nand_4_out,
       nand_5_out, nand_7_out, nand_8_out, nand_9_out, nand_10_out, nand_11_out;

  nand nand_1 (nand_1_out, X, X);
  nand nand_2 (nand_2_out, JK2_q, JK3_qn);
  nand nand_3 (nand_3_out, nand_1_out, JK1_qn, JK2_qn, JK3_q);
  nand nand_4 (nand_4_out, X, JK1_qn);
  nand nand_5 (nand_5_out, nand_1_out, JK1_q, JK2_qn);
  nand nand_6 (Y, nand_2_out, nand_2_out);
  nand nand_7 (nand_7_out, nand_3_out, nand_3_out);
  nand nand_8 (nand_8_out, nand_1_out, JK3_q);
  nand nand_9 (nand_9_out, nand_3_out, nand_1_out);
  nand nand_10 (nand_10_out, nand_4_out, JK2_qn);
  nand nand_11 (nand_11_out, nand_5_out, nand_5_out);
  J_K_Flip_Flop JK1 (
    .J(nand_7_out), .clk(CLK), .K(nand_8_out), .Q(JK1_q), .Qn(JK1_qn), .reset(RST));  // open: preset, en
  J_K_Flip_Flop JK2 (
    .J(nand_9_out), .clk(CLK), .K(nand_1_out), .Q(JK2_q), .Qn(JK2_qn), .reset(RST));  // open: preset, en
  J_K_Flip_Flop JK3 (
    .J(nand_10_out), .clk(CLK), .K(nand_11_out), .Q(JK3_q), .Qn(JK3_qn), .reset(RST));  // open: preset, en
endmodule
